// Logisim project f1-model.circ as structural Verilog: 3 circuits, main circuit Main
module Main (
  input  in_1
);

  wire A, A_O, ADD, ADR_H, ADR_L, ADR_SEL, ALU, BR, BRC, BRZ, CLK, controlled_buffer_1_out, LD, MAR, MDA,
       MEM_out, MV_IMM4, MV_REG, NOT, not_1_out, not_2_out, not_3_out, OR, or_1_out, or_2_out, PC, PC_HI_O,
       PC_LD, PC_LO_O, PC_out, POP, pull_resistor_1_node, pull_resistor_2_node, pull_resistor_3_node,
       pull_resistor_4_node, pull_resistor_5_node, pull_resistor_6_node, pull_resistor_7_node,
       pull_resistor_8_node, pull_resistor_9_node, pull_resistor_10_node, pull_resistor_11_node,
       pull_resistor_12_node, pull_resistor_13_node, pull_resistor_14_node, pull_resistor_15_node,
       pull_resistor_16_node, pull_resistor_17_node, pull_resistor_18_node, pull_resistor_19_node,
       pull_resistor_20_node, pull_resistor_21_node, pull_resistor_22_node, pull_resistor_23_node,
       pull_resistor_24_node, pull_resistor_25_node, pull_resistor_26_node, pull_resistor_27_node,
       pull_resistor_28_node, pull_resistor_29_node, pull_resistor_30_node, pull_resistor_31_node,
       pull_resistor_32_node, pull_resistor_33_node, pull_resistor_34_node, pull_resistor_35_node,
       pull_resistor_36_node, pull_resistor_37_node, pull_resistor_38_node, pull_resistor_39_node,
       pull_resistor_40_node, pull_resistor_41_node, pull_resistor_42_node, pull_resistor_43_node,
       pull_resistor_44_node, pull_resistor_45_node, pull_resistor_46_node, pull_resistor_47_node,
       pull_resistor_48_node, pull_resistor_49_node, pull_resistor_50_node, pull_resistor_51_node,
       pull_resistor_52_node, pull_resistor_53_node, pull_resistor_54_node, pull_resistor_55_node, PUSH, RAM,
       RAM_LD, REG, REG_O, REG_SEL, ROM, SP, SP_DEC, SP_O, ST, SUB, T1, T2, T3, T4, T5, T6, T7, undriven, Z_O;
  wire [1:0] ALU_FUN;
  wire [3:0] A__IN_OUT, A_ALU, ADR_H_q, alu_1_out, alu_1_zvc, ALU_flags, controlled_buffer_173_out, MDA_q,
       ram_1_data, ram_2_data, REG_SEL_q, rom_1_data, SP_q, Z_q;
  wire [3:2] IR__OUT;
  wire [7:0] ADR, ADR__OUT, multiplexer_1_out, PC__OUT;

  Pull_Resistor pull_resistor_1 (.node(pull_resistor_1_node));
  Pull_Resistor pull_resistor_2 (.node(pull_resistor_2_node));
  Pull_Resistor pull_resistor_3 (.node(pull_resistor_3_node));
  Pull_Resistor pull_resistor_4 (.node(pull_resistor_4_node));
  Pull_Resistor pull_resistor_5 (.node(pull_resistor_5_node));
  Pull_Resistor pull_resistor_6 (.node(pull_resistor_6_node));
  Pull_Resistor pull_resistor_7 (.node(pull_resistor_7_node));
  Pull_Resistor pull_resistor_8 (.node(pull_resistor_8_node));
  Pull_Resistor pull_resistor_9 (.node(pull_resistor_9_node));
  Pull_Resistor pull_resistor_10 (.node(pull_resistor_10_node));
  Pull_Resistor pull_resistor_11 (.node(pull_resistor_11_node));
  Pull_Resistor pull_resistor_12 (.node(pull_resistor_12_node));
  Pull_Resistor pull_resistor_13 (.node(pull_resistor_13_node));
  Pull_Resistor pull_resistor_14 (.node(pull_resistor_14_node));
  Pull_Resistor pull_resistor_15 (.node(pull_resistor_15_node));
  Pull_Resistor pull_resistor_16 (.node(pull_resistor_16_node));
  Pull_Resistor pull_resistor_17 (.node(pull_resistor_17_node));
  assign controlled_buffer_1_out = undriven ? undriven : 1'bz;  // Controlled_Buffer controlled_buffer_1
  Pull_Resistor pull_resistor_18 (.node(pull_resistor_18_node));
  Pull_Resistor pull_resistor_19 (.node(pull_resistor_19_node));
  Pull_Resistor pull_resistor_20 (.node(pull_resistor_20_node));
  Pull_Resistor pull_resistor_21 (.node(pull_resistor_21_node));
  Pull_Resistor pull_resistor_22 (.node(pull_resistor_22_node));
  Pull_Resistor pull_resistor_23 (.node(pull_resistor_23_node));
  Pull_Resistor pull_resistor_24 (.node(pull_resistor_24_node));
  Pull_Resistor pull_resistor_25 (.node(pull_resistor_25_node));
  Pull_Resistor pull_resistor_26 (.node(pull_resistor_26_node));
  Pull_Resistor pull_resistor_27 (.node(pull_resistor_27_node));
  Pull_Resistor pull_resistor_28 (.node(pull_resistor_28_node));
  Pull_Resistor pull_resistor_29 (.node(pull_resistor_29_node));
  Pull_Resistor pull_resistor_30 (.node(pull_resistor_30_node));
  Pull_Resistor pull_resistor_31 (.node(pull_resistor_31_node));
  Pull_Resistor pull_resistor_32 (.node(pull_resistor_32_node));
  Pull_Resistor pull_resistor_33 (.node(pull_resistor_33_node));
  Pull_Resistor pull_resistor_34 (.node(pull_resistor_34_node));
  Pull_Resistor pull_resistor_35 (.node(pull_resistor_35_node));
  Pull_Resistor pull_resistor_36 (.node(pull_resistor_36_node));
  Pull_Resistor pull_resistor_37 (.node(pull_resistor_37_node));
  Pull_Resistor pull_resistor_38 (.node(pull_resistor_38_node));
  Pull_Resistor pull_resistor_39 (.node(pull_resistor_39_node));
  Pull_Resistor pull_resistor_40 (.node(pull_resistor_40_node));
  Pull_Resistor pull_resistor_41 (.node(pull_resistor_41_node));
  Pull_Resistor pull_resistor_42 (.node(pull_resistor_42_node));
  Pull_Resistor pull_resistor_43 (.node(pull_resistor_43_node));
  Pull_Resistor pull_resistor_44 (.node(pull_resistor_44_node));
  Pull_Resistor pull_resistor_45 (.node(pull_resistor_45_node));
  Pull_Resistor pull_resistor_46 (.node(pull_resistor_46_node));
  Pull_Resistor pull_resistor_47 (.node(pull_resistor_47_node));
  Pull_Resistor pull_resistor_48 (.node(pull_resistor_48_node));
  Pull_Resistor pull_resistor_49 (.node(pull_resistor_49_node));
  Pull_Resistor pull_resistor_50 (.node(pull_resistor_50_node));
  Pull_Resistor pull_resistor_51 (.node(pull_resistor_51_node));
  Pull_Resistor pull_resistor_52 (.node(pull_resistor_52_node));
  Pull_Resistor pull_resistor_53 (.node(pull_resistor_53_node));
  Pull_Resistor pull_resistor_54 (.node(pull_resistor_54_node));
  Pull_Resistor pull_resistor_55 (.node(pull_resistor_55_node));
  assign PC_LD = pull_resistor_20_node ? pull_resistor_20_node : 1'bz;  // Controlled_Buffer controlled_buffer_2
  assign PC_LD = pull_resistor_48_node ? pull_resistor_48_node : 1'bz;  // Controlled_Buffer controlled_buffer_3
  assign PC_LD = pull_resistor_53_node ? pull_resistor_53_node : 1'bz;  // Controlled_Buffer controlled_buffer_4
  Pull_Resistor pull_resistor_56 (.node(PC_LD));
  Pull_Resistor pull_resistor_57 (.node(PC));
  Clock clock_1 (.out(CLK));
  Squencer squencer_1 (
    .CLK(CLK), .ENBL(1'b1), .RST(in_1), .T1(T1), .T2(T2), .T3(T3), .T4(T4), .T5(T5), .T6(T6), .T7(T7));  // open: T8
  buf buffer_1 (MAR, pull_resistor_1_node);
  assign PC = pull_resistor_2_node ? pull_resistor_2_node : 1'bz;  // Controlled_Buffer controlled_buffer_5
  buf buffer_2 (MAR, pull_resistor_2_node);
  assign PC = pull_resistor_3_node ? pull_resistor_3_node : 1'bz;  // Controlled_Buffer controlled_buffer_6
  buf buffer_3 (MAR, pull_resistor_3_node);
  buf buffer_4 (MAR, pull_resistor_4_node);
  assign PC = pull_resistor_4_node ? pull_resistor_4_node : 1'bz;  // Controlled_Buffer controlled_buffer_7
  buf buffer_5 (MAR, pull_resistor_6_node);
  buf buffer_6 (MAR, pull_resistor_7_node);
  assign PC = pull_resistor_7_node ? pull_resistor_7_node : 1'bz;  // Controlled_Buffer controlled_buffer_8
  assign PC = pull_resistor_8_node ? pull_resistor_8_node : 1'bz;  // Controlled_Buffer controlled_buffer_9
  buf buffer_7 (MAR, pull_resistor_8_node);
  buf buffer_8 (MAR, pull_resistor_9_node);
  assign PC = pull_resistor_9_node ? pull_resistor_9_node : 1'bz;  // Controlled_Buffer controlled_buffer_10
  buf buffer_9 (MAR, pull_resistor_11_node);
  assign PC = pull_resistor_12_node ? pull_resistor_12_node : 1'bz;  // Controlled_Buffer controlled_buffer_11
  assign MAR = pull_resistor_12_node ? pull_resistor_12_node : 1'bz;  // Controlled_Buffer controlled_buffer_12
  assign PC = pull_resistor_13_node ? pull_resistor_13_node : 1'bz;  // Controlled_Buffer controlled_buffer_13
  assign A_O = pull_resistor_13_node ? pull_resistor_13_node : 1'bz;  // Controlled_Buffer controlled_buffer_14
  assign MAR = pull_resistor_14_node ? pull_resistor_14_node : 1'bz;  // Controlled_Buffer controlled_buffer_15
  assign PC = pull_resistor_15_node ? pull_resistor_15_node : 1'bz;  // Controlled_Buffer controlled_buffer_16
  assign MAR = pull_resistor_16_node ? pull_resistor_16_node : 1'bz;  // Controlled_Buffer controlled_buffer_17
  assign PC = pull_resistor_17_node ? pull_resistor_17_node : 1'bz;  // Controlled_Buffer controlled_buffer_18
  assign A_O = pull_resistor_17_node ? pull_resistor_17_node : 1'bz;  // Controlled_Buffer controlled_buffer_19
  assign MAR = pull_resistor_18_node ? pull_resistor_18_node : 1'bz;  // Controlled_Buffer controlled_buffer_20
  assign PC = pull_resistor_19_node ? pull_resistor_19_node : 1'bz;  // Controlled_Buffer controlled_buffer_21
  assign MAR = pull_resistor_19_node ? pull_resistor_19_node : 1'bz;  // Controlled_Buffer controlled_buffer_22
  assign MAR = pull_resistor_22_node ? pull_resistor_22_node : 1'bz;  // Controlled_Buffer controlled_buffer_23
  assign MAR = pull_resistor_23_node ? pull_resistor_23_node : 1'bz;  // Controlled_Buffer controlled_buffer_24
  assign PC = pull_resistor_24_node ? pull_resistor_24_node : 1'bz;  // Controlled_Buffer controlled_buffer_25
  assign MAR = pull_resistor_25_node ? pull_resistor_25_node : 1'bz;  // Controlled_Buffer controlled_buffer_26
  assign MAR = pull_resistor_26_node ? pull_resistor_26_node : 1'bz;  // Controlled_Buffer controlled_buffer_27
  assign PC = pull_resistor_27_node ? pull_resistor_27_node : 1'bz;  // Controlled_Buffer controlled_buffer_28
  assign MAR = pull_resistor_28_node ? pull_resistor_28_node : 1'bz;  // Controlled_Buffer controlled_buffer_29
  assign PC = pull_resistor_29_node ? pull_resistor_29_node : 1'bz;  // Controlled_Buffer controlled_buffer_30
  assign MAR = pull_resistor_30_node ? pull_resistor_30_node : 1'bz;  // Controlled_Buffer controlled_buffer_31
  assign PC = pull_resistor_31_node ? pull_resistor_31_node : 1'bz;  // Controlled_Buffer controlled_buffer_32
  assign MAR = pull_resistor_33_node ? pull_resistor_33_node : 1'bz;  // Controlled_Buffer controlled_buffer_33
  assign PC = pull_resistor_34_node ? pull_resistor_34_node : 1'bz;  // Controlled_Buffer controlled_buffer_34
  assign MAR = pull_resistor_35_node ? pull_resistor_35_node : 1'bz;  // Controlled_Buffer controlled_buffer_35
  assign PC = pull_resistor_36_node ? pull_resistor_36_node : 1'bz;  // Controlled_Buffer controlled_buffer_36
  assign MAR = pull_resistor_38_node ? pull_resistor_38_node : 1'bz;  // Controlled_Buffer controlled_buffer_37
  assign PC = pull_resistor_39_node ? pull_resistor_39_node : 1'bz;  // Controlled_Buffer controlled_buffer_38
  assign MAR = pull_resistor_40_node ? pull_resistor_40_node : 1'bz;  // Controlled_Buffer controlled_buffer_39
  assign PC = pull_resistor_41_node ? pull_resistor_41_node : 1'bz;  // Controlled_Buffer controlled_buffer_40
  assign MAR = pull_resistor_43_node ? pull_resistor_43_node : 1'bz;  // Controlled_Buffer controlled_buffer_41
  assign PC = pull_resistor_44_node ? pull_resistor_44_node : 1'bz;  // Controlled_Buffer controlled_buffer_42
  assign MAR = pull_resistor_46_node ? pull_resistor_46_node : 1'bz;  // Controlled_Buffer controlled_buffer_43
  assign MAR = pull_resistor_47_node ? pull_resistor_47_node : 1'bz;  // Controlled_Buffer controlled_buffer_44
  assign PC = pull_resistor_49_node ? pull_resistor_49_node : 1'bz;  // Controlled_Buffer controlled_buffer_45
  assign PC = pull_resistor_50_node ? pull_resistor_50_node : 1'bz;  // Controlled_Buffer controlled_buffer_46
  assign MAR = pull_resistor_51_node ? pull_resistor_51_node : 1'bz;  // Controlled_Buffer controlled_buffer_47
  assign MAR = pull_resistor_52_node ? pull_resistor_52_node : 1'bz;  // Controlled_Buffer controlled_buffer_48
  assign PC = pull_resistor_54_node ? pull_resistor_54_node : 1'bz;  // Controlled_Buffer controlled_buffer_49
  assign PC = pull_resistor_55_node ? pull_resistor_55_node : 1'bz;  // Controlled_Buffer controlled_buffer_50
  Pull_Resistor pull_resistor_58 (.node(A_O));
  Pull_Resistor pull_resistor_59 (.node(MAR));
  Multiplexer #(.width(8)) multiplexer_1 (
    .in0(PC__OUT), .in1(ADR__OUT), .out(multiplexer_1_out), .sel(ADR_SEL));  // open: en
  or or_1 (or_1_out, T1, MAR);
  assign ROM = pull_resistor_1_node ? pull_resistor_1_node : 1'bz;  // Controlled_Buffer controlled_buffer_51
  assign ROM = pull_resistor_2_node ? pull_resistor_2_node : 1'bz;  // Controlled_Buffer controlled_buffer_52
  assign REG_SEL = pull_resistor_3_node ? pull_resistor_3_node : 1'bz;  // Controlled_Buffer controlled_buffer_53
  assign ROM = pull_resistor_3_node ? pull_resistor_3_node : 1'bz;  // Controlled_Buffer controlled_buffer_54
  assign REG_SEL = pull_resistor_6_node ? pull_resistor_6_node : 1'bz;  // Controlled_Buffer controlled_buffer_55
  assign ROM = pull_resistor_6_node ? pull_resistor_6_node : 1'bz;  // Controlled_Buffer controlled_buffer_56
  assign ROM = pull_resistor_7_node ? pull_resistor_7_node : 1'bz;  // Controlled_Buffer controlled_buffer_57
  assign ROM = pull_resistor_8_node ? pull_resistor_8_node : 1'bz;  // Controlled_Buffer controlled_buffer_58
  assign A = pull_resistor_11_node ? pull_resistor_11_node : 1'bz;  // Controlled_Buffer controlled_buffer_59
  assign ROM = pull_resistor_11_node ? pull_resistor_11_node : 1'bz;  // Controlled_Buffer controlled_buffer_60
  assign ROM = pull_resistor_12_node ? pull_resistor_12_node : 1'bz;  // Controlled_Buffer controlled_buffer_61
  assign REG_SEL = pull_resistor_12_node ? pull_resistor_12_node : 1'bz;  // Controlled_Buffer controlled_buffer_62
  assign ROM = pull_resistor_14_node ? pull_resistor_14_node : 1'bz;  // Controlled_Buffer controlled_buffer_63
  assign REG_SEL = pull_resistor_14_node ? pull_resistor_14_node : 1'bz;  // Controlled_Buffer controlled_buffer_64
  assign A = pull_resistor_15_node ? pull_resistor_15_node : 1'bz;  // Controlled_Buffer controlled_buffer_65
  assign ROM = pull_resistor_16_node ? pull_resistor_16_node : 1'bz;  // Controlled_Buffer controlled_buffer_66
  assign REG_SEL = pull_resistor_16_node ? pull_resistor_16_node : 1'bz;  // Controlled_Buffer controlled_buffer_67
  assign ROM = pull_resistor_18_node ? pull_resistor_18_node : 1'bz;  // Controlled_Buffer controlled_buffer_68
  assign ROM = pull_resistor_19_node ? pull_resistor_19_node : 1'bz;  // Controlled_Buffer controlled_buffer_69
  assign ROM = pull_resistor_22_node ? pull_resistor_22_node : 1'bz;  // Controlled_Buffer controlled_buffer_70
  assign REG_SEL = pull_resistor_22_node ? pull_resistor_22_node : 1'bz;  // Controlled_Buffer controlled_buffer_71
  assign ROM = pull_resistor_25_node ? pull_resistor_25_node : 1'bz;  // Controlled_Buffer controlled_buffer_72
  assign REG_SEL = pull_resistor_25_node ? pull_resistor_25_node : 1'bz;  // Controlled_Buffer controlled_buffer_73
  assign REG_SEL = pull_resistor_28_node ? pull_resistor_28_node : 1'bz;  // Controlled_Buffer controlled_buffer_74
  assign ROM = pull_resistor_28_node ? pull_resistor_28_node : 1'bz;  // Controlled_Buffer controlled_buffer_75
  assign A = pull_resistor_29_node ? pull_resistor_29_node : 1'bz;  // Controlled_Buffer controlled_buffer_76
  assign REG_SEL = pull_resistor_30_node ? pull_resistor_30_node : 1'bz;  // Controlled_Buffer controlled_buffer_77
  assign ROM = pull_resistor_30_node ? pull_resistor_30_node : 1'bz;  // Controlled_Buffer controlled_buffer_78
  assign REG_SEL = pull_resistor_33_node ? pull_resistor_33_node : 1'bz;  // Controlled_Buffer controlled_buffer_79
  assign ROM = pull_resistor_33_node ? pull_resistor_33_node : 1'bz;  // Controlled_Buffer controlled_buffer_80
  assign A = pull_resistor_34_node ? pull_resistor_34_node : 1'bz;  // Controlled_Buffer controlled_buffer_81
  assign ROM = pull_resistor_35_node ? pull_resistor_35_node : 1'bz;  // Controlled_Buffer controlled_buffer_82
  assign REG_SEL = pull_resistor_35_node ? pull_resistor_35_node : 1'bz;  // Controlled_Buffer controlled_buffer_83
  assign REG_SEL = pull_resistor_38_node ? pull_resistor_38_node : 1'bz;  // Controlled_Buffer controlled_buffer_84
  assign ROM = pull_resistor_38_node ? pull_resistor_38_node : 1'bz;  // Controlled_Buffer controlled_buffer_85
  assign A = pull_resistor_39_node ? pull_resistor_39_node : 1'bz;  // Controlled_Buffer controlled_buffer_86
  assign ROM = pull_resistor_40_node ? pull_resistor_40_node : 1'bz;  // Controlled_Buffer controlled_buffer_87
  assign REG_SEL = pull_resistor_40_node ? pull_resistor_40_node : 1'bz;  // Controlled_Buffer controlled_buffer_88
  assign ROM = pull_resistor_43_node ? pull_resistor_43_node : 1'bz;  // Controlled_Buffer controlled_buffer_89
  assign REG_SEL = pull_resistor_43_node ? pull_resistor_43_node : 1'bz;  // Controlled_Buffer controlled_buffer_90
  assign ROM = pull_resistor_46_node ? pull_resistor_46_node : 1'bz;  // Controlled_Buffer controlled_buffer_91
  assign ROM = pull_resistor_47_node ? pull_resistor_47_node : 1'bz;  // Controlled_Buffer controlled_buffer_92
  assign ROM = pull_resistor_51_node ? pull_resistor_51_node : 1'bz;  // Controlled_Buffer controlled_buffer_93
  assign ROM = pull_resistor_52_node ? pull_resistor_52_node : 1'bz;  // Controlled_Buffer controlled_buffer_94
  Pull_Resistor pull_resistor_60 (.node(REG_SEL));
  Pull_Resistor pull_resistor_61 (.node(A));
  Pull_Resistor pull_resistor_62 (.node(ROM));
  Register #(.trigger("high")) u_MAR (.D(multiplexer_1_out), .en(or_1_out), .Q(ADR), .clk(CLK), .clr(in_1));
  assign REG = pull_resistor_5_node ? pull_resistor_5_node : 1'bz;  // Controlled_Buffer controlled_buffer_95
  assign REG = pull_resistor_10_node ? pull_resistor_10_node : 1'bz;  // Controlled_Buffer controlled_buffer_96
  assign REG_O = pull_resistor_10_node ? pull_resistor_10_node : 1'bz;  // Controlled_Buffer controlled_buffer_97
  assign REG = pull_resistor_13_node ? pull_resistor_13_node : 1'bz;  // Controlled_Buffer controlled_buffer_98
  assign REG_O = pull_resistor_15_node ? pull_resistor_15_node : 1'bz;  // Controlled_Buffer controlled_buffer_99
  assign REG = pull_resistor_15_node ? pull_resistor_15_node : 1'bz;  // Controlled_Buffer controlled_buffer_100
  assign REG = pull_resistor_17_node ? pull_resistor_17_node : 1'bz;  // Controlled_Buffer controlled_buffer_101
  assign REG_O = pull_resistor_24_node ? pull_resistor_24_node : 1'bz;  // Controlled_Buffer controlled_buffer_102
  assign REG = pull_resistor_24_node ? pull_resistor_24_node : 1'bz;  // Controlled_Buffer controlled_buffer_103
  assign REG = pull_resistor_27_node ? pull_resistor_27_node : 1'bz;  // Controlled_Buffer controlled_buffer_104
  assign REG_O = pull_resistor_29_node ? pull_resistor_29_node : 1'bz;  // Controlled_Buffer controlled_buffer_105
  assign REG = pull_resistor_29_node ? pull_resistor_29_node : 1'bz;  // Controlled_Buffer controlled_buffer_106
  assign REG_O = pull_resistor_31_node ? pull_resistor_31_node : 1'bz;  // Controlled_Buffer controlled_buffer_107
  assign REG = pull_resistor_31_node ? pull_resistor_31_node : 1'bz;  // Controlled_Buffer controlled_buffer_108
  assign REG = pull_resistor_32_node ? pull_resistor_32_node : 1'bz;  // Controlled_Buffer controlled_buffer_109
  assign REG = pull_resistor_34_node ? pull_resistor_34_node : 1'bz;  // Controlled_Buffer controlled_buffer_110
  assign REG_O = pull_resistor_34_node ? pull_resistor_34_node : 1'bz;  // Controlled_Buffer controlled_buffer_111
  assign REG = pull_resistor_36_node ? pull_resistor_36_node : 1'bz;  // Controlled_Buffer controlled_buffer_112
  assign REG_O = pull_resistor_36_node ? pull_resistor_36_node : 1'bz;  // Controlled_Buffer controlled_buffer_113
  assign REG = pull_resistor_37_node ? pull_resistor_37_node : 1'bz;  // Controlled_Buffer controlled_buffer_114
  assign REG = pull_resistor_39_node ? pull_resistor_39_node : 1'bz;  // Controlled_Buffer controlled_buffer_115
  assign REG_O = pull_resistor_39_node ? pull_resistor_39_node : 1'bz;  // Controlled_Buffer controlled_buffer_116
  assign REG = pull_resistor_41_node ? pull_resistor_41_node : 1'bz;  // Controlled_Buffer controlled_buffer_117
  assign REG_O = pull_resistor_41_node ? pull_resistor_41_node : 1'bz;  // Controlled_Buffer controlled_buffer_118
  assign REG = pull_resistor_42_node ? pull_resistor_42_node : 1'bz;  // Controlled_Buffer controlled_buffer_119
  assign REG = pull_resistor_44_node ? pull_resistor_44_node : 1'bz;  // Controlled_Buffer controlled_buffer_120
  assign REG_O = pull_resistor_44_node ? pull_resistor_44_node : 1'bz;  // Controlled_Buffer controlled_buffer_121
  assign REG = pull_resistor_45_node ? pull_resistor_45_node : 1'bz;  // Controlled_Buffer controlled_buffer_122
  Pull_Resistor pull_resistor_63 (.node(REG_O));
  Pull_Resistor pull_resistor_64 (.node(MDA));
  Pull_Resistor pull_resistor_65 (.node(REG));
  or MEM (MEM_out, T1, ROM);
  assign MDA = pull_resistor_1_node ? pull_resistor_1_node : 1'bz;  // Controlled_Buffer controlled_buffer_123
  assign ADR_H = pull_resistor_1_node ? pull_resistor_1_node : 1'bz;  // Controlled_Buffer controlled_buffer_124
  assign ADR_L = pull_resistor_2_node ? pull_resistor_2_node : 1'bz;  // Controlled_Buffer controlled_buffer_125
  assign MDA = pull_resistor_2_node ? pull_resistor_2_node : 1'bz;  // Controlled_Buffer controlled_buffer_126
  assign MDA = pull_resistor_3_node ? pull_resistor_3_node : 1'bz;  // Controlled_Buffer controlled_buffer_127
  assign MDA = pull_resistor_4_node ? pull_resistor_4_node : 1'bz;  // Controlled_Buffer controlled_buffer_128
  assign MDA = pull_resistor_5_node ? pull_resistor_5_node : 1'bz;  // Controlled_Buffer controlled_buffer_129
  assign MDA = pull_resistor_6_node ? pull_resistor_6_node : 1'bz;  // Controlled_Buffer controlled_buffer_130
  assign ADR_H = pull_resistor_7_node ? pull_resistor_7_node : 1'bz;  // Controlled_Buffer controlled_buffer_131
  assign MDA = pull_resistor_7_node ? pull_resistor_7_node : 1'bz;  // Controlled_Buffer controlled_buffer_132
  assign MDA = pull_resistor_8_node ? pull_resistor_8_node : 1'bz;  // Controlled_Buffer controlled_buffer_133
  assign ADR_L = pull_resistor_8_node ? pull_resistor_8_node : 1'bz;  // Controlled_Buffer controlled_buffer_134
  assign MDA = pull_resistor_11_node ? pull_resistor_11_node : 1'bz;  // Controlled_Buffer controlled_buffer_135
  assign MDA = pull_resistor_12_node ? pull_resistor_12_node : 1'bz;  // Controlled_Buffer controlled_buffer_136
  assign MDA = pull_resistor_14_node ? pull_resistor_14_node : 1'bz;  // Controlled_Buffer controlled_buffer_137
  assign MDA = pull_resistor_16_node ? pull_resistor_16_node : 1'bz;  // Controlled_Buffer controlled_buffer_138
  assign MDA = pull_resistor_18_node ? pull_resistor_18_node : 1'bz;  // Controlled_Buffer controlled_buffer_139
  assign ADR_H = pull_resistor_18_node ? pull_resistor_18_node : 1'bz;  // Controlled_Buffer controlled_buffer_140
  assign ADR_L = pull_resistor_19_node ? pull_resistor_19_node : 1'bz;  // Controlled_Buffer controlled_buffer_141
  assign MDA = pull_resistor_19_node ? pull_resistor_19_node : 1'bz;  // Controlled_Buffer controlled_buffer_142
  assign MDA = pull_resistor_22_node ? pull_resistor_22_node : 1'bz;  // Controlled_Buffer controlled_buffer_143
  assign ADR_L = pull_resistor_23_node ? pull_resistor_23_node : 1'bz;  // Controlled_Buffer controlled_buffer_144
  assign MDA = pull_resistor_25_node ? pull_resistor_25_node : 1'bz;  // Controlled_Buffer controlled_buffer_145
  assign ADR_L = pull_resistor_26_node ? pull_resistor_26_node : 1'bz;  // Controlled_Buffer controlled_buffer_146
  assign MDA = pull_resistor_27_node ? pull_resistor_27_node : 1'bz;  // Controlled_Buffer controlled_buffer_147
  assign MDA = pull_resistor_28_node ? pull_resistor_28_node : 1'bz;  // Controlled_Buffer controlled_buffer_148
  assign MDA = pull_resistor_30_node ? pull_resistor_30_node : 1'bz;  // Controlled_Buffer controlled_buffer_149
  assign MDA = pull_resistor_33_node ? pull_resistor_33_node : 1'bz;  // Controlled_Buffer controlled_buffer_150
  assign MDA = pull_resistor_35_node ? pull_resistor_35_node : 1'bz;  // Controlled_Buffer controlled_buffer_151
  assign MDA = pull_resistor_38_node ? pull_resistor_38_node : 1'bz;  // Controlled_Buffer controlled_buffer_152
  assign MDA = pull_resistor_40_node ? pull_resistor_40_node : 1'bz;  // Controlled_Buffer controlled_buffer_153
  assign MDA = pull_resistor_43_node ? pull_resistor_43_node : 1'bz;  // Controlled_Buffer controlled_buffer_154
  assign MDA = pull_resistor_46_node ? pull_resistor_46_node : 1'bz;  // Controlled_Buffer controlled_buffer_155
  assign ADR_H = pull_resistor_46_node ? pull_resistor_46_node : 1'bz;  // Controlled_Buffer controlled_buffer_156
  assign MDA = pull_resistor_47_node ? pull_resistor_47_node : 1'bz;  // Controlled_Buffer controlled_buffer_157
  assign ADR_L = pull_resistor_47_node ? pull_resistor_47_node : 1'bz;  // Controlled_Buffer controlled_buffer_158
  assign ADR_H = pull_resistor_51_node ? pull_resistor_51_node : 1'bz;  // Controlled_Buffer controlled_buffer_159
  assign MDA = pull_resistor_51_node ? pull_resistor_51_node : 1'bz;  // Controlled_Buffer controlled_buffer_160
  assign MDA = pull_resistor_52_node ? pull_resistor_52_node : 1'bz;  // Controlled_Buffer controlled_buffer_161
  assign ADR_L = pull_resistor_52_node ? pull_resistor_52_node : 1'bz;  // Controlled_Buffer controlled_buffer_162
  Pull_Resistor pull_resistor_66 (.node(ADR_H));
  Pull_Resistor pull_resistor_67 (.node(ADR_L));
  ROM #(.dataWidth(4)) rom_1 (.addr(ADR), .data(rom_1_data), .sel(MEM_out));
  assign RAM_LD = pull_resistor_4_node ? pull_resistor_4_node : 1'bz;  // Controlled_Buffer controlled_buffer_163
  assign RAM = pull_resistor_4_node ? pull_resistor_4_node : 1'bz;  // Controlled_Buffer controlled_buffer_164
  assign ADR_SEL = pull_resistor_4_node ? pull_resistor_4_node : 1'bz;  // Controlled_Buffer controlled_buffer_165
  assign ADR_SEL = pull_resistor_9_node ? pull_resistor_9_node : 1'bz;  // Controlled_Buffer controlled_buffer_166
  assign RAM = pull_resistor_10_node ? pull_resistor_10_node : 1'bz;  // Controlled_Buffer controlled_buffer_167
  assign ADR_SEL = pull_resistor_23_node ? pull_resistor_23_node : 1'bz;  // Controlled_Buffer controlled_buffer_168
  assign RAM = pull_resistor_24_node ? pull_resistor_24_node : 1'bz;  // Controlled_Buffer controlled_buffer_169
  assign ADR_SEL = pull_resistor_26_node ? pull_resistor_26_node : 1'bz;  // Controlled_Buffer controlled_buffer_170
  assign RAM = pull_resistor_27_node ? pull_resistor_27_node : 1'bz;  // Controlled_Buffer controlled_buffer_171
  assign RAM_LD = pull_resistor_27_node ? pull_resistor_27_node : 1'bz;  // Controlled_Buffer controlled_buffer_172
  Pull_Resistor pull_resistor_68 (.node(RAM));
  Pull_Resistor pull_resistor_69 (.node(ADR_SEL));
  Pull_Resistor pull_resistor_70 (.node(RAM_LD));
  assign controlled_buffer_173_out = MEM_out ? rom_1_data : 4'bz;  // Controlled_Buffer controlled_buffer_173
  or or_2 (or_2_out, T1, MDA);
  assign controlled_buffer_173_out = RAM_LD ? ram_1_data : 4'bz;  // Controlled_Buffer controlled_buffer_174
  RAM #(.dataWidth(4)) ram_1 (.addr(ADR), .data(ram_1_data), .sel(RAM), .clk(CLK), .ld(RAM_LD), .clr(in_1));
  assign ram_1_data = not_1_out ? A__IN_OUT : 4'bz;  // Controlled_Buffer controlled_buffer_175
  not not_1 (not_1_out, RAM_LD);
  assign SP = pull_resistor_24_node ? pull_resistor_24_node : 1'bz;  // Controlled_Buffer controlled_buffer_176
  assign SP_DEC = pull_resistor_25_node ? pull_resistor_25_node : 1'bz;  // Controlled_Buffer controlled_buffer_177
  assign SP = pull_resistor_25_node ? pull_resistor_25_node : 1'bz;  // Controlled_Buffer controlled_buffer_178
  Pull_Resistor pull_resistor_71 (.node(SP_DEC));
  Pull_Resistor pull_resistor_72 (.node(SP));
  Pull_Resistor pull_resistor_73 (.node(SP_O));
  Register #(.width(4), .trigger("high")) u_MDA (
    .D(controlled_buffer_173_out), .en(or_2_out), .Q(MDA_q), .clk(CLK), .clr(in_1));
  assign A__IN_OUT = or_2_out ? MDA_q : 4'bz;  // Controlled_Buffer controlled_buffer_179
  assign SP_O = pull_resistor_23_node ? pull_resistor_23_node : 1'bz;  // Controlled_Buffer controlled_buffer_180
  assign SP_O = pull_resistor_26_node ? pull_resistor_26_node : 1'bz;  // Controlled_Buffer controlled_buffer_181
  Pull_Resistor pull_resistor_74 (.node(PC_LO_O));
  Pull_Resistor pull_resistor_75 (.node(PC_HI_O));
  and and_1 (pull_resistor_1_node, LD, T3);
  and and_2 (pull_resistor_2_node, LD, T4);
  and and_3 (pull_resistor_3_node, LD, T5);
  and and_4 (pull_resistor_4_node, LD, T6);
  and and_5 (pull_resistor_5_node, LD, T7);
  and and_6 (pull_resistor_6_node, ST, T3);
  and and_7 (pull_resistor_7_node, ST, T4);
  and and_8 (pull_resistor_8_node, ST, T5);
  and and_9 (pull_resistor_9_node, ST, T6);
  and and_10 (pull_resistor_10_node, ST, T7);
  and and_11 (pull_resistor_11_node, MV_IMM4, T3);
  and and_12 (pull_resistor_12_node, MV_IMM4, T4);
  and and_13 (pull_resistor_13_node, MV_IMM4, T5);
  and and_14 (pull_resistor_14_node, MV_REG, T3);
  and and_15 (pull_resistor_15_node, MV_REG, T4);
  and and_16 (pull_resistor_16_node, MV_REG, T5);
  and and_17 (pull_resistor_17_node, MV_REG, T6);
  and and_18 (pull_resistor_18_node, BR, T3);
  and and_19 (pull_resistor_19_node, BR, T4);
  and and_20 (pull_resistor_20_node, BR, T5);
  and and_21 (pull_resistor_21_node, BR, T6);
  and and_22 (pull_resistor_22_node, PUSH, T3);
  and and_23 (pull_resistor_23_node, PUSH, T4);
  and and_24 (pull_resistor_24_node, PUSH, T5);
  and and_25 (pull_resistor_25_node, POP, T3);
  and and_26 (pull_resistor_26_node, POP, T4);
  and and_27 (pull_resistor_27_node, POP, T5);
  and and_28 (pull_resistor_28_node, ADD, T3);
  and and_29 (pull_resistor_29_node, ADD, T4);
  and and_30 (pull_resistor_30_node, ADD, T5);
  assign ALU = pull_resistor_31_node ? pull_resistor_31_node : 1'bz;  // Controlled_Buffer controlled_buffer_182
  and and_31 (pull_resistor_31_node, ADD, T6);
  assign Z_O = pull_resistor_32_node ? pull_resistor_32_node : 1'bz;  // Controlled_Buffer controlled_buffer_183
  and and_32 (pull_resistor_32_node, ADD, T7);
  and and_33 (pull_resistor_33_node, SUB, T3);
  and and_34 (pull_resistor_34_node, SUB, T4);
  and and_35 (pull_resistor_35_node, SUB, T5);
  assign ALU = pull_resistor_36_node ? pull_resistor_36_node : 1'bz;  // Controlled_Buffer controlled_buffer_184
  and and_36 (pull_resistor_36_node, SUB, T6);
  assign Z_O = pull_resistor_37_node ? pull_resistor_37_node : 1'bz;  // Controlled_Buffer controlled_buffer_185
  and and_37 (pull_resistor_37_node, SUB, T7);
  and and_38 (pull_resistor_38_node, OR, T3);
  and and_39 (pull_resistor_39_node, OR, T4);
  and and_40 (pull_resistor_40_node, OR, T5);
  assign ALU = pull_resistor_41_node ? pull_resistor_41_node : 1'bz;  // Controlled_Buffer controlled_buffer_186
  and and_41 (pull_resistor_41_node, OR, T6);
  assign Z_O = pull_resistor_42_node ? pull_resistor_42_node : 1'bz;  // Controlled_Buffer controlled_buffer_187
  and and_42 (pull_resistor_42_node, OR, T7);
  and and_43 (pull_resistor_43_node, NOT, T3);
  assign ALU = pull_resistor_44_node ? pull_resistor_44_node : 1'bz;  // Controlled_Buffer controlled_buffer_188
  and and_44 (pull_resistor_44_node, NOT, T4);
  assign Z_O = pull_resistor_45_node ? pull_resistor_45_node : 1'bz;  // Controlled_Buffer controlled_buffer_189
  and and_45 (pull_resistor_45_node, NOT, T5);
  and and_46 (pull_resistor_46_node, BRZ, ALU_flags[2], T3);
  and and_47 (pull_resistor_47_node, BRZ, ALU_flags[2], T4);
  and and_48 (pull_resistor_48_node, BRZ, ALU_flags[2], T6);
  and and_49 (pull_resistor_49_node, BRZ, T4);
  and and_50 (pull_resistor_50_node, BRZ, T5);
  and and_51 (pull_resistor_51_node, BRC, ALU_flags[2], T3);
  and and_52 (pull_resistor_52_node, BRC, ALU_flags[2], T4);
  and and_53 (pull_resistor_53_node, BRC, ALU_flags[2], T6);
  and and_54 (pull_resistor_54_node, BRC, T4);
  and and_55 (pull_resistor_55_node, BRC, T5);
  Pull_Resistor pull_resistor_76 (.node(ALU));
  Pull_Resistor pull_resistor_77 (.node(Z_O));
  Pull_Resistor pull_resistor_78 (.node(T3));
  Pull_Resistor pull_resistor_79 (.node(T4));
  Pull_Resistor pull_resistor_80 (.node(T5));
  Register #(.width(4), .trigger("high")) u_REG_SEL (.D(A__IN_OUT), .en(REG_SEL), .Q(REG_SEL_q), .clk(CLK), .clr(in_1));
  Pull_Resistor pull_resistor_81 (.node(T7));
  Pull_Resistor pull_resistor_82 (.node(T6));
  Counter #(.width(4), .max('hf)) u_SP (.load(SP_DEC), .count(SP), .Q(SP_q), .clk(CLK), .clr(in_1));  // open: D, carry
  assign A__IN_OUT = SP_O ? SP_q : 4'bz;  // Controlled_Buffer controlled_buffer_190
  Pull_Resistor pull_resistor_83 (.node(ALU_flags[2]));
  Pull_Resistor pull_resistor_84 (.node(ALU_flags[1]));
  Pull_Resistor pull_resistor_85 (.node(ALU_flags[3]));
  RAM #(.addrWidth(4), .dataWidth(4), .bus("asynch")) ram_2 (
    .addr(REG_SEL_q), .data(ram_2_data), .sel(REG), .ld(REG_O), .clr(in_1));
  assign ram_2_data = not_2_out ? A__IN_OUT : 4'bz;  // Controlled_Buffer controlled_buffer_191
  not not_2 (not_2_out, REG_O);
  assign A__IN_OUT = REG_O ? ram_2_data : 4'bz;  // Controlled_Buffer controlled_buffer_192
  Pull_Resistor pull_resistor_86 (.node(ALU_flags[0]));
  Register #(.width(4), .trigger("high")) u_ADR_H (.D(A__IN_OUT), .en(ADR_H), .Q(ADR_H_q), .clk(CLK), .clr(in_1));
  Register #(.width(4), .trigger("high")) u_ADR_L (.D(A__IN_OUT), .en(ADR_L), .Q(ADR__OUT[3:0]), .clk(CLK), .clr(in_1));
  Register #(.width(4), .trigger("high")) u_A (.D(A__IN_OUT), .en(A), .Q(A_ALU), .clk(CLK), .clr(in_1));
  assign ADR__OUT[7:4] = SP_O ? 4'b0000 : 4'bz;  // Controlled_Buffer controlled_buffer_193
  assign ADR__OUT[7:4] = not_3_out ? ADR_H_q : 4'bz;  // Controlled_Buffer controlled_buffer_194
  not not_3 (not_3_out, SP_O);
  assign A__IN_OUT = A_O ? A_ALU : 4'bz;  // Controlled_Buffer controlled_buffer_195
  Register #(.width(4), .trigger("high")) FLAGS (.D(alu_1_zvc), .en(ALU), .Q(ALU_flags), .clk(CLK), .clr(in_1));
  ALU alu_1 (.CTRL(ALU_FUN), .EN(ALU), .A(A_ALU), .DTA(A__IN_OUT), .OUT(alu_1_out), .ZVC(alu_1_zvc));
  Decoder #(.select(4)) decoder_1 (
    .out0(LD), .out1(ST), .out2(MV_IMM4), .out3(MV_REG), .out4(BR), .out5(PUSH), .out6(POP), .out8(ADD),
    .out9(SUB), .out10(OR), .out11(NOT), .out12(BRZ), .out13(BRC), .sel({IR__OUT, ALU_FUN}));  // open: out7, out14, out15, en
  Register #(.width(4)) Z (.D(alu_1_out), .en(ALU), .Q(Z_q), .clk(CLK), .clr(in_1));
  assign A__IN_OUT = Z_O ? Z_q : 4'bz;  // Controlled_Buffer controlled_buffer_196
  or u_PC (PC_out, T2, PC);
  Register #(.width(4), .trigger("high")) IR (.D(A__IN_OUT), .en(T1), .Q({IR__OUT, ALU_FUN}), .clk(CLK), .clr(in_1));
  Counter PC_2 (.load(PC_LD), .D(ADR__OUT), .count(PC_out), .Q(PC__OUT), .clk(CLK), .clr(in_1));  // open: carry
  assign A__IN_OUT = PC_LO_O ? PC__OUT[3:0] : 4'bz;  // Controlled_Buffer controlled_buffer_197
  assign A__IN_OUT = PC_HI_O ? PC__OUT[7:4] : 4'bz;  // Controlled_Buffer controlled_buffer_198

  // Other names for the same wires on the sheet: IR__OUT[1:0] = ALU_FUN; RST = in_1; ADR_HI__IN[3:0] = A__IN_OUT;
  //   ADR_LO__IN[3:0] = A__IN_OUT; ALU__IN[3:0] = A__IN_OUT; DTA[3:0] = A__IN_OUT; IR__IN[3:0] = A__IN_OUT;
  //   PC_HI__OUT[3:0] = A__IN_OUT; PC_LOW__OUT[3:0] = A__IN_OUT; REG_SEL__IN[3:0] = A__IN_OUT;
  //   REGS__IN_OUT[3:0] = A__IN_OUT; SP__OUT[3:0] = A__IN_OUT; Z__OUT[3:0] = A__IN_OUT

  // Notes on the sheet:
  //   buffer_1 drives only 1 and floats otherwise
  //   buffer_2 drives only 1 and floats otherwise
  //   buffer_3 drives only 1 and floats otherwise
  //   buffer_4 drives only 1 and floats otherwise
  //   buffer_5 drives only 1 and floats otherwise
  //   buffer_6 drives only 1 and floats otherwise
  //   buffer_7 drives only 1 and floats otherwise
  //   buffer_8 drives only 1 and floats otherwise
  //   buffer_9 drives only 1 and floats otherwise
  //   contents of rom_1 (hex, n*v repeats v):
  //   2 0 2 2 1 1 2 a 0 8 1 2 9 0 1 3 1 0 2 1 1 c 1 b 4 0 9 8 1 0 9 2 1 3 1 2 2 1 1 c 2 d 4 1 b 4 0 9
  //   REGS
  //   O
  //   Z
  //   C
endmodule

// sequencer
module Squencer (
  input  CLK,
  input  ENBL,
  input  RST,
  output T1,
  output T2,
  output T3,
  output T4,
  output T5,
  output T6,
  output T7,
  output T8
);

  wire [2:0] j_k_ff_1_q;

  J_K_Flip_Flop #(.trigger("falling")) j_k_ff_1 (
    .J(ENBL), .clk(CLK), .K(ENBL), .Q(j_k_ff_1_q[0]), .en(ENBL), .reset(RST));  // open: Qn, preset
  Decoder #(.select(3)) decoder_1 (
    .out0(T1), .out1(T2), .out2(T3), .out3(T4), .out4(T5), .out5(T6), .out6(T7), .out7(T8), .sel(j_k_ff_1_q),
    .en(ENBL));
  J_K_Flip_Flop #(.trigger("falling")) j_k_ff_2 (
    .J(ENBL), .clk(j_k_ff_1_q[0]), .K(ENBL), .Q(j_k_ff_1_q[1]), .en(ENBL), .reset(RST));  // open: Qn, preset
  J_K_Flip_Flop #(.trigger("falling")) j_k_ff_3 (
    .J(ENBL), .clk(j_k_ff_1_q[1]), .K(ENBL), .Q(j_k_ff_1_q[2]), .en(ENBL), .reset(RST));  // open: Qn, preset
endmodule

module ALU (
  input  [1:0] CTRL,
  input  EN,
  input  [3:0] A,
  input  [3:0] DTA,
  output [3:0] ZVC,
  output [3:0] OUT
);

  wire ADD, NOT, OR, SUB;
  wire [3:0] adder_1_out, controlled_buffer_3_out, controlled_buffer_4_out, controlled_buffer_5_out,
       controlled_buffer_7_out, not_1_out, pull_resistor_2_node, pull_resistor_4_node, pull_resistor_12_node,
       pull_resistor_16_node, subtractor_1_out;

  Decoder #(.select(2)) decoder_1 (.out0(ADD), .out1(SUB), .out2(OR), .out3(NOT), .sel(CTRL), .en(EN));
  Pull_Resistor pull_resistor_1 (.node(ADD));
  Pull_Resistor pull_resistor_2 (.node(pull_resistor_2_node));
  assign pull_resistor_2_node = ADD ? A : 4'bz;  // Controlled_Buffer controlled_buffer_1
  Pull_Resistor pull_resistor_3 (.node(ADD));
  Pull_Resistor pull_resistor_4 (.node(pull_resistor_4_node));
  assign pull_resistor_4_node = ADD ? DTA : 4'bz;  // Controlled_Buffer controlled_buffer_2
  Pull_Resistor pull_resistor_5 (.node(SUB));
  assign controlled_buffer_3_out = SUB ? A : 4'bz;  // Controlled_Buffer controlled_buffer_3
  Pull_Resistor pull_resistor_6 (.node(controlled_buffer_3_out));
  Pull_Resistor pull_resistor_7 (.node(SUB));
  assign controlled_buffer_4_out = SUB ? DTA : 4'bz;  // Controlled_Buffer controlled_buffer_4
  Pull_Resistor pull_resistor_8 (.node(controlled_buffer_4_out));
  Pull_Resistor pull_resistor_9 (.node(OR));
  assign controlled_buffer_5_out = OR ? A : 4'bz;  // Controlled_Buffer controlled_buffer_5
  Pull_Resistor pull_resistor_10 (.node(controlled_buffer_5_out));
  Pull_Resistor pull_resistor_11 (.node(OR));
  Pull_Resistor pull_resistor_12 (.node(pull_resistor_12_node));
  assign pull_resistor_12_node = OR ? DTA : 4'bz;  // Controlled_Buffer controlled_buffer_6
  Pull_Resistor pull_resistor_13 (.node(NOT));
  assign controlled_buffer_7_out = NOT ? DTA : 4'bz;  // Controlled_Buffer controlled_buffer_7
  Pull_Resistor pull_resistor_14 (.node(controlled_buffer_7_out));
  Adder #(.width(4)) adder_1 (
    .a(pull_resistor_2_node), .b(pull_resistor_4_node), .out(adder_1_out), .cout(ZVC[0]));  // open: cin
  Pull_Resistor pull_resistor_15 (.node(ZVC[0]));
  Subtractor #(.width(4)) subtractor_1 (
    .a(controlled_buffer_3_out), .b(controlled_buffer_4_out), .out(subtractor_1_out), .bout(ZVC[1]));  // open: bin
  Pull_Resistor pull_resistor_16 (.node(pull_resistor_16_node));
  assign pull_resistor_16_node = controlled_buffer_5_out | pull_resistor_12_node;  // OR_Gate or_1, 4 bits wide
  assign not_1_out = ~controlled_buffer_7_out;  // NOT_Gate not_1, 4 bits wide
  Pull_Resistor pull_resistor_17 (.node(ZVC[3]));
  and and_1 (ZVC[2], ~OUT[3], ~OUT[2], ~OUT[1], ~OUT[0]);  // AND_Gate
  Multiplexer #(.select(2), .width(4)) multiplexer_1 (
    .in0(adder_1_out), .in1(subtractor_1_out), .in2(pull_resistor_16_node), .in3(not_1_out), .out(OUT),
    .sel(CTRL), .en(EN));
  Pull_Resistor pull_resistor_18 (.node(OUT));
endmodule
